# Fritzing sketch periph-circuit (saved by Fritzing 0.9.3b)
breadboards: 1

parts:
  TRRS_cable = TRRS 3.5mm Jack Breakout
  R1 = Resistor [tolerance=±5% resistance=10k package="0402 [SMD]"]
  R2 = Resistor [tolerance=±5% resistance=2k package="0402 [SMD]"]
  R3 = Resistor [tolerance=±5% resistance=2k package="0402 [SMD]"]
  C1 = Electrolytic Capacitor [capacitance=1μF package="0405 [SMD, electrolytic]"]
  Microcontroller = Arduino Uno (Rev3)

nets:
  N1: TRRS_cable.SLEEVE, R2.Pin_1, R3.Pin_1, Microcontroller.GND
  N2: TRRS_cable.RING2, R3.Pin_0, C1.-
  N3: R1.Pin_0, R2.Pin_0, C1.+
  N4: R1.Pin_1, Microcontroller.D8
